// Logisim project 4. modul.circ as structural Verilog: 1 circuit, main circuit main
module main (
  input  D,
  input  C,
  input  B,
  input  A,
  input  D_2,
  input  C_2,
  input  B_2,
  input  A_2,
  output Y,
  output y_2
);

  wire and_1_out, and_2_out, and_3_out, and_4_out, and_5_out, or_2_out, or_3_out, or_4_out, or_5_out,
       or_6_out, or_7_out, or_8_out, or_9_out, or_10_out, or_11_out, or_12_out;

  and and_1 (and_1_out, ~D, C, B, A);  // AND_Gate
  and and_2 (and_2_out, D, ~C, B, A);  // AND_Gate
  and and_3 (and_3_out, D, C, ~B, A);  // AND_Gate
  and and_4 (and_4_out, D, C, B, ~A);  // AND_Gate
  and and_5 (and_5_out, D, C, B, A);
  or or_1 (Y, and_1_out, and_2_out, and_3_out, and_4_out, and_5_out);
  or or_2 (or_2_out, D_2, C_2, B_2, A_2);
  or or_3 (or_3_out, D_2, C_2, B_2, ~A_2);  // OR_Gate
  or or_4 (or_4_out, D_2, C_2, ~B_2, A_2);  // OR_Gate
  or or_5 (or_5_out, D_2, C_2, ~B_2, ~A_2);  // OR_Gate
  or or_6 (or_6_out, D_2, ~C_2, B_2, A_2);  // OR_Gate
  or or_7 (or_7_out, D_2, ~C_2, B_2, ~A_2);  // OR_Gate
  or or_8 (or_8_out, D_2, ~C_2, ~B_2, A_2);  // OR_Gate
  or or_9 (or_9_out, ~D_2, C_2, B_2, A_2);  // OR_Gate
  or or_10 (or_10_out, ~D_2, C_2, B_2, ~A_2);  // OR_Gate
  or or_11 (or_11_out, ~D_2, C_2, ~B_2, A_2);  // OR_Gate
  or or_12 (or_12_out, ~D_2, ~C_2, B_2, A_2);  // OR_Gate
  and and_6 (y_2, or_2_out, or_3_out, or_4_out, or_5_out, or_6_out, or_7_out, or_8_out, or_9_out, or_10_out, or_11_out, or_12_out);

  // Notes on the sheet:
  //   Diszjunktív kanonikus alak
  //   Konjunktív kanonikus alak
endmodule
