// Logisim project 7. modul minta áramkör.circ as structural Verilog: 1 circuit, main circuit main
module main (
  input  ENP,
  input  ENT,
  input  RES,
  output QD,
  output QC,
  output QB,
  output QA,
  output TC
);

  wire and_1_out, and_3_out, \ellenállás_1_p5 , \ellenállás_1_p8 , n162_dec_count_sync_clear_1_p6,
       n162_dec_count_sync_clear_1_p8, nor_1_out;

  and and_1 (and_1_out, QD, ~QC, ~QB, ~QA);  // AND_Gate
  nor nor_1 (nor_1_out, and_1_out, RES);
  // ellenállás ellenállás_1: pin names not known; wires that end beside it: nor_1_out, ENP, ENT, 1'b1, \ellenállás_1_p5 , 1'b0, \ellenállás_1_p5 , \ellenállás_1_p8 
  and and_2 (\ellenállás_1_p8 , ~QD, QC, ~QB, QA);  // AND_Gate
  and and_3 (and_3_out, ~QD, ~QC, QB, ~QA);  // AND_Gate
  // _162_Dec_Count_Sync_Clear 162_dec_count_sync_clear_1: pin names not known; wires that end beside it: QD, QC, QB, \ellenállás_1_p8 , QA, n162_dec_count_sync_clear_1_p6, TC, n162_dec_count_sync_clear_1_p8
  nor nor_2 (n162_dec_count_sync_clear_1_p6, and_3_out, \ellenállás_1_p8 );
  Clock CLK (.out(n162_dec_count_sync_clear_1_p8));

  // Notes on the sheet:
  //   +UT
endmodule
